# Fritzing sketch reset_button (saved by Fritzing 0.9.6b)

parts:
  Raspberry_Pi_1 = Raspberry Pi 3 [part_number=RPI-3-V1.2]
  Reset_Button = Pushbutton [package="[THT]"]

nets:
  N1: Raspberry_Pi_1.GND, Reset_Button.Pin_1, Reset_Button.Pin_2
  N2: Raspberry_Pi_1.GPIO23, Reset_Button.Pin_3, Reset_Button.Pin_4
